# Fritzing sketch robot_wiring (saved by Fritzing 0.9.5d)
breadboards: 1

parts:
  Part1 = Arduino Nano (Rev3.0) (ICSP)
  Part3 = NRF24L01+ Breakout Board
  C1 = Electrolytic Capacitor [capacitance=100μF package="0807 [SMD, electrolytic]"]
  J1 = Basic Servo

nets:
  GND: Part1.GND, Part3.GND, C1.-, J1.gnd
  N1: Part1.D11/MOSI, Part3.MOSI
  N2: Part1.D12/MISO, Part3.MISO
  5V: Part1.5V, J1.vcc
  N3: Part1.A2, J1.pulse
  N4: Part1.A1, Part3.CS
  N5: Part1.A0, Part3.CE
  3V3: Part1.3V3, Part3.VCC, C1.+
  N6: Part1.D13/SCK, Part3.SCK
