# Fritzing sketch transmitter (saved by Fritzing 0.9.5d)
breadboards: 1

parts:
  Part1 = Arduino Nano (Rev3.0) (ICSP)
  Part3 = NRF24L01+ Breakout Board
  C1 = Electrolytic Capacitor [capacitance=100μF package="0807 [SMD, electrolytic]"]
  Mod1 = KY-023 Dual Axis Joystick Module [package="Breakout board"]
  Mod2 = KY-023 Dual Axis Joystick Module [package="Breakout board"]

nets:
  GND: Part1.GND, Part3.GND, C1.-, Mod1.GND, Mod2.GND
  N1: Part1.D7, Mod2.SW
  N2: Part1.D8, Mod1.SW
  N3: Part1.D9, Part3.CS
  N4: Part1.D10, Part3.CE
  N5: Part1.D11/MOSI, Part3.MOSI
  N6: Part1.D12/MISO, Part3.MISO
  +5V: Part1.5V, Mod1.+5V, Mod2.+5V
  N7: Part1.A3, Mod2.VRx
  N8: Part1.A2, Mod2.VRy
  N9: Part1.A1, Mod1.VRx
  N10: Part1.A0, Mod1.VRy
  3V3: Part1.3V3, Part3.VCC, C1.+
  N11: Part1.D13/SCK, Part3.SCK

custom parts:
  KY-023 Dual Axis Joystick Module: KY-023 Dual-Axis Joystick Module.
